// Logisim project Processor.circ as structural Verilog
module IF (
  input  [23:0] branchTarget,
  input  isBranchTaken,
  input  IFstageclock,
  input  reset,
  output [31:0] Instruction,
  output [23:0] PC
);

  wire and_1_out, multiplexer_1_out, not_1_out, not_2_out;

  not not_1 (not_1_out, IFstageclock);
  not not_2 (not_2_out, isBranchTaken);
  Multiplexer #(.enable("false")) multiplexer_1 (.in0(not_1_out), .in1(1'b1), .out(multiplexer_1_out), .sel(and_1_out));
  Counter #(.width(24), .max('hffffff)) counter_1 (
    .load(isBranchTaken), .D(branchTarget), .count(not_2_out), .Q(PC), .clk(multiplexer_1_out), .clr(reset));  // open: carry
  ROM #(.addrWidth(24), .dataWidth(32)) rom_1 (.addr(PC), .data(Instruction));  // open: sel
  and and_1 (and_1_out, Instruction[31], Instruction[30], Instruction[29], Instruction[28], Instruction[27], Instruction[26], Instruction[25], Instruction[24], Instruction[23], Instruction[22], Instruction[21], Instruction[20], Instruction[19], Instruction[18], Instruction[17], Instruction[16], Instruction[14], Instruction[13], Instruction[12], Instruction[11], Instruction[10], Instruction[9], Instruction[8], Instruction[7], Instruction[6], Instruction[5], Instruction[4], Instruction[3], Instruction[2], Instruction[1], Instruction[0], Instruction[15]);

  // Notes on the sheet:
  //   reset: pull=down
  //   IF Stage
  //   Counter for going to the next instruction
  //   Note: The last instruction should be provided as "ffffffff" otherwise it will keep on interpreting "00000000", i.e. it will keep on doubling r0.
  //   contents of rom_1 (hex, n*v repeats v):
  //   4c000173 4c400000 48800000 4d400000 90000007 24c8000a 110cc000 1110c000 1550000 1c88000a 90000001
  //   2c080000 8ffffff9 80000001 28140000 80000002 90000002 4c400001 90000000 ffffffff
  //   Used to stop instruction processing on encountering code "ffffffff".
endmodule

module OF (
  input  isRet,
  input  [23:0] PC,
  input  isImmx,
  input  [31:0] Instruction,
  input  isCall,
  input  Mux1,
  input  [3:0] writeAddress,
  input  [31:0] writeData,
  input  isWb,
  input  clock,
  input  isSt,
  input  [3:0] displayAddress,
  input  Mux2,
  output [31:0] A,
  output [31:0] op2,
  output [31:0] B,
  output [31:0] displayOut,
  output [31:0] branchTarget
);

  wire and_1_out, or_1_out;
  wire [3:0] multiplexer_2_out, multiplexer_3_out;
  wire [31:0] adder_1_out, bit_extender_1_out, bit_extender_2_out, bit_extender_3_out, bit_extender_4_out,
       immx, regfile_1_outa, regfile_1_outb, shifter_1_out;

  assign bit_extender_1_out = {{5{Instruction[26]}}, Instruction[26:0]};  // Bit_Extender bit_extender_1
  assign bit_extender_2_out = {{8{1'b0}}, PC};  // Bit_Extender bit_extender_2
  Multiplexer #(.width(32), .enable("false")) multiplexer_1 (
    .in0(adder_1_out), .in1(A), .out(branchTarget), .sel(isRet));
  Adder #(.width(32)) adder_1 (.a(bit_extender_1_out), .b(bit_extender_2_out), .out(adder_1_out));  // open: cin, cout
  assign bit_extender_3_out = {{16{Instruction[15]}}, Instruction[15:0]};  // Bit_Extender bit_extender_3
  assign bit_extender_4_out = {{16{1'b0}}, Instruction[15:0]};  // Bit_Extender bit_extender_4
  Shifter #(.width(32)) shifter_1 (.in(bit_extender_4_out), .\dist (5'b10000), .out(shifter_1_out));
  Multiplexer #(.width(4), .enable("false")) multiplexer_2 (
    .in0(Instruction[21:18]), .in1(4'b1111), .out(multiplexer_2_out), .sel(isRet));
  Multiplexer #(.width(4), .enable("false")) multiplexer_3 (
    .in0(Instruction[17:14]), .in1(Instruction[25:22]), .out(multiplexer_3_out), .sel(isSt));
  Multiplexer #(.select(2), .width(32), .enable("false")) multiplexer_4 (
    .in0(bit_extender_3_out), .in1(bit_extender_4_out), .in2(shifter_1_out), .out(immx),
    .sel(Instruction[17:16]));  // open: in3
  regFile regfile_1 (
    .writeData(writeData), .writeAddress(writeAddress), .clock(and_1_out), .readB(multiplexer_3_out),
    .outB(regfile_1_outb), .outA(regfile_1_outa), .readA(multiplexer_2_out), .displayOut(displayOut),
    .displayRead(displayAddress));
  and and_1 (and_1_out, or_1_out, clock);
  or or_1 (or_1_out, isCall, isWb);
  Multiplexer #(.width(32), .enable("false")) multiplexer_5 (.in0(op2), .in1(immx), .out(B), .sel(isImmx));
  Multiplexer #(.width(32), .enable("false")) multiplexer_6 (
    .in0(regfile_1_outb), .in1(writeData), .out(op2), .sel(Mux2));
  Multiplexer #(.width(32), .enable("false")) multiplexer_7 (
    .in0(regfile_1_outa), .in1(writeData), .out(A), .sel(Mux1));

  // Other names for the same wires on the sheet: muxedop2[31:0] = op2

  // Notes on the sheet:
  //   (Branch Target Calculation)
  //   (27 bit offset)
  //   OF Stage (Edited)
  //   (has Return Address
  //   when instruction is ret)
  //   (Registers from RW Stage moved here to maintain consistency)
  //   rs1
  //   rs2
  //   rd
  //   (modifier bits)
  //   19:22
  //   15:18
  //   23:26
  //   (Immediate Calculation)
  //   (no modifier)
  //   (modifier u)
  //   (modifier h)
  //   (Register Access)
  //   (32 bit modifed immediate)
  //   (OF Outputs)
endmodule

module MA (
  input  [31:0] ALUResult,
  input  isLd,
  input  Clock,
  input  isSt,
  input  Mux6,
  input  [31:0] op2,
  input  [31:0] Forwarded_Data,
  output [31:0] ldResult
);

  wire and_1_out, not_1_out, xor_1_out;
  wire [31:0] multiplexer_1_out, shifter_1_out;

  Shifter #(.width(32), .shift("ar")) shifter_1 (.in(ALUResult), .\dist (5'b00010), .out(shifter_1_out));
  and and_1 (and_1_out, isSt, Clock);
  xor xor_1 (xor_1_out, isLd, and_1_out);
  not not_1 (not_1_out, isSt);
  RAM #(.addrWidth(24), .dataWidth(32), .bus("asynch")) ram_1 (
    .addr(shifter_1_out[23:0]), .data(ldResult), .sel(xor_1_out), .ld(not_1_out));  // open: clr
  assign ldResult = isSt ? multiplexer_1_out : 32'bz;  // Controlled_Buffer controlled_buffer_1
  Multiplexer #(.width(32), .enable("false")) multiplexer_1 (
    .in0(op2), .in1(Forwarded_Data), .out(multiplexer_1_out), .sel(Mux6));

  // Notes on the sheet:
  //   MA  Stage
  //   Memory Address
  //   (Data to be stored)
endmodule

module RW (
  input  [31:0] ALUResult,
  input  [31:0] ldResult,
  input  isLd,
  input  [23:0] PC,
  input  isCall,
  input  [31:0] Instruction,
  output [31:0] storeData,
  output [3:0] Address
);

  wire [31:0] adder_1_out, bit_extender_1_out;

  assign bit_extender_1_out = {{8{1'b0}}, PC};  // Bit_Extender bit_extender_1
  Multiplexer #(.width(4), .enable("false")) multiplexer_1 (
    .in0(Instruction[25:22]), .in1(4'b1111), .out(Address), .sel(isCall));
  Adder #(.width(32)) adder_1 (.a(bit_extender_1_out), .b(32'h1), .out(adder_1_out));  // open: cin, cout
  Multiplexer #(.select(2), .width(32), .enable("false")) multiplexer_2 (
    .in0(ALUResult), .in1(ldResult), .in2(adder_1_out), .out(storeData), .sel({isCall, isLd}));  // open: in3

  // Notes on the sheet:
  //   PC: pull=down
  //   storeData: pull=down
  //   Address: pull=down
  //   RW Stage (Edited)
  //   (for arithmetic instructions)
  //   (data loaded from memory)
  //   (to update return address)
  //   (Register to be written to)
  //   (Registers moved to OF Stage to maintain consistency)
  //   (Integer to be written back in register)
endmodule

module regFile (
  input  clock,
  input  [3:0] readA,
  input  [31:0] writeData,
  input  [3:0] readB,
  input  [3:0] writeAddress,
  input  [3:0] displayRead,
  output [31:0] outA,
  output [31:0] outB,
  output [31:0] displayOut
);

  wire counter_1_q;
  wire [31:0] demultiplexer_1_out0, demultiplexer_1_out1, demultiplexer_1_out2, demultiplexer_1_out3,
       demultiplexer_1_out4, demultiplexer_1_out5, demultiplexer_1_out6, demultiplexer_1_out7,
       demultiplexer_1_out8, demultiplexer_1_out9, demultiplexer_1_out10, demultiplexer_1_out11,
       demultiplexer_1_out12, demultiplexer_1_out13, demultiplexer_1_out14, demultiplexer_1_out15,
       multiplexer_1_out, r0, r1, r2, r3, r4, r5, r6, r7, r8, r9, r10, r11, r12, r13, r14, r15;

  Demultiplexer #(.select(4), .width(32), .tristate("true"), .enable("false")) demultiplexer_1 (
    .out0(demultiplexer_1_out0), .out1(demultiplexer_1_out1), .out2(demultiplexer_1_out2),
    .out3(demultiplexer_1_out3), .out4(demultiplexer_1_out4), .out5(demultiplexer_1_out5),
    .out6(demultiplexer_1_out6), .out7(demultiplexer_1_out7), .out8(demultiplexer_1_out8),
    .out9(demultiplexer_1_out9), .out10(demultiplexer_1_out10), .out11(demultiplexer_1_out11),
    .out12(demultiplexer_1_out12), .out13(demultiplexer_1_out13), .out14(demultiplexer_1_out14),
    .out15(demultiplexer_1_out15), .in(writeData), .sel(writeAddress));
  Counter #(.width(1), .max('h1), .ongoal("stay")) counter_1 (
    .Q(counter_1_q), .clk(clock));  // open: load, D, count, carry, clr
  Multiplexer #(.width(32), .enable("false")) multiplexer_1 (
    .in0(32'h3fffffc), .in1(demultiplexer_1_out14), .out(multiplexer_1_out), .sel(counter_1_q));
  Register #(.width(32)) u_r0 (.D(demultiplexer_1_out0), .Q(r0), .clk(clock));  // open: en, clr
  Register #(.width(32)) u_r1 (.D(demultiplexer_1_out1), .Q(r1), .clk(clock));  // open: en, clr
  Register #(.width(32)) u_r2 (.D(demultiplexer_1_out2), .Q(r2), .clk(clock));  // open: en, clr
  Register #(.width(32)) u_r3 (.D(demultiplexer_1_out3), .Q(r3), .clk(clock));  // open: en, clr
  Register #(.width(32)) u_r4 (.D(demultiplexer_1_out4), .Q(r4), .clk(clock));  // open: en, clr
  Register #(.width(32)) u_r5 (.D(demultiplexer_1_out5), .Q(r5), .clk(clock));  // open: en, clr
  Register #(.width(32)) u_r6 (.D(demultiplexer_1_out6), .Q(r6), .clk(clock));  // open: en, clr
  Register #(.width(32)) u_r7 (.D(demultiplexer_1_out7), .Q(r7), .clk(clock));  // open: en, clr
  Register #(.width(32)) u_r8 (.D(demultiplexer_1_out8), .Q(r8), .clk(clock));  // open: en, clr
  Register #(.width(32)) u_r9 (.D(demultiplexer_1_out9), .Q(r9), .clk(clock));  // open: en, clr
  Register #(.width(32)) u_r10 (.D(demultiplexer_1_out10), .Q(r10), .clk(clock));  // open: en, clr
  Register #(.width(32)) u_r11 (.D(demultiplexer_1_out11), .Q(r11), .clk(clock));  // open: en, clr
  Register #(.width(32)) u_r12 (.D(demultiplexer_1_out12), .Q(r12), .clk(clock));  // open: en, clr
  Register #(.width(32)) u_r13 (.D(demultiplexer_1_out13), .Q(r13), .clk(clock));  // open: en, clr
  Register #(.width(32)) u_r14 (.D(multiplexer_1_out), .Q(r14), .clk(clock));  // open: en, clr
  Register #(.width(32)) u_r15 (.D(demultiplexer_1_out15), .Q(r15), .clk(clock));  // open: en, clr
  Multiplexer #(.select(4), .width(32), .disabled(0), .enable("false")) multiplexer_2 (
    .in0(r0), .in1(r1), .in2(r2), .in3(r3), .in4(r4), .in5(r5), .in6(r6), .in7(r7), .in8(r8), .in9(r9),
    .in10(r10), .in11(r11), .in12(r12), .in13(r13), .in14(r14), .in15(r15), .out(outA), .sel(readA));
  Multiplexer #(.select(4), .width(32), .disabled(0), .enable("false")) multiplexer_3 (
    .in0(r0), .in1(r1), .in2(r2), .in3(r3), .in4(r4), .in5(r5), .in6(r6), .in7(r7), .in8(r8), .in9(r9),
    .in10(r10), .in11(r11), .in12(r12), .in13(r13), .in14(r14), .in15(r15), .out(outB), .sel(readB));
  Multiplexer #(.select(4), .width(32), .disabled(0), .enable("false")) multiplexer_4 (
    .in0(r0), .in1(r1), .in2(r2), .in3(r3), .in4(r4), .in5(r5), .in6(r6), .in7(r7), .in8(r8), .in9(r9),
    .in10(r10), .in11(r11), .in12(r12), .in13(r13), .in14(r14), .in15(r15), .out(displayOut),
    .sel(displayRead));

  // Notes on the sheet:
  //   writeAddress: pull=down
  //   displayOut: pull=down
  //   outB: pull=down
  //   outA: pull=down
  //   displayRead: pull=down
  //   writeData: pull=down
  //   readB: pull=down
  //   readA: pull=down
  //   (for RW Stage)
  //   (to initialize stack pointer
  //   to last memory location)
  //   (to fetch Operand 1)
  //   (to fetch Operand 2)
  //   (for external display)
endmodule

module CU (
  input  [31:0] Instruction,
  output isWb,
  output isUbranch,
  output isImmediate,
  output isLd,
  output isSt,
  output isBeq,
  output isBgt,
  output isCall,
  output isRet,
  output [3:0] ALUSignals
);

  wire and_1_out, and_2_out, and_3_out, and_4_out, demultiplexer_1_out0, demultiplexer_1_out1, isAdd, isAnd,
       isAsr, isCmp, isDiv, isLsl, isLsr, isMod, isMov, isMul, isNot, isOr, not_1_out, not_2_out, not_3_out,
       not_4_out, not_5_out, not_6_out, not_7_out, or_1_out, or_2_out;
  wire [3:0] adder_1_out, adder_2_out, adder_3_out, adder_4_out, adder_5_out, adder_6_out, adder_7_out,
       adder_8_out, adder_9_out, adder_10_out, adder_11_out, bit_extender_1_out, bit_extender_2_out,
       bit_extender_3_out, bit_extender_4_out, bit_extender_5_out, bit_extender_6_out, bit_extender_7_out,
       bit_extender_8_out, bit_extender_9_out, bit_extender_10_out, bit_extender_11_out, bit_extender_12_out,
       bit_extender_13_out, multiplier_1_out, multiplier_2_out, multiplier_3_out, multiplier_4_out,
       multiplier_5_out, multiplier_6_out, multiplier_7_out, multiplier_8_out, multiplier_9_out,
       multiplier_10_out, multiplier_11_out, multiplier_12_out;

  not not_1 (not_1_out, Instruction[28]);
  not not_2 (not_2_out, Instruction[29]);
  not not_3 (not_3_out, Instruction[28]);
  not not_4 (not_4_out, Instruction[27]);
  not not_5 (not_5_out, Instruction[31]);
  Demultiplexer #(.select(5), .disabled(0), .enable("false")) demultiplexer_1 (
    .out0(demultiplexer_1_out0), .out1(demultiplexer_1_out1), .out2(isMul), .out3(isDiv), .out4(isMod),
    .out5(isCmp), .out6(isAnd), .out7(isOr), .out8(isNot), .out9(isMov), .out10(isLsl), .out11(isLsr),
    .out12(isAsr), .out14(isLd), .out15(isSt), .out16(isBeq), .out17(isBgt), .out19(isCall), .out20(isRet),
    .in(1'b1), .sel(Instruction[31:27]));  // open: out13, out18, out21, out22, out23, out24, out25, out26, out27, out28, out29, out30, out31
  not not_6 (not_6_out, Instruction[31]);
  or or_1 (or_1_out, Instruction[30], not_1_out);
  and and_1 (and_1_out, not_2_out, Instruction[28]);
  and and_2 (and_2_out, Instruction[29], not_3_out, not_4_out);
  and and_3 (and_3_out, Instruction[28], Instruction[29], Instruction[30], not_5_out);
  and and_4 (and_4_out, not_6_out, Instruction[29], Instruction[27], or_1_out);
  not not_7 (not_7_out, Instruction[30]);
  or or_2 (or_2_out, and_1_out, and_2_out);
  nor nor_1 (isWb, Instruction[31], and_4_out);
  and and_5 (isUbranch, Instruction[31], not_7_out, or_2_out);
  or or_3 (isAdd, and_3_out, demultiplexer_1_out0);
  assign bit_extender_1_out = {{3{1'b0}}, demultiplexer_1_out1};  // Bit_Extender bit_extender_1
  assign bit_extender_2_out = {{3{1'b0}}, isCmp};  // Bit_Extender bit_extender_2
  assign bit_extender_3_out = {{3{1'b0}}, isMul};  // Bit_Extender bit_extender_3
  assign bit_extender_4_out = {{3{1'b0}}, isDiv};  // Bit_Extender bit_extender_4
  assign bit_extender_5_out = {{3{1'b0}}, isMod};  // Bit_Extender bit_extender_5
  assign bit_extender_6_out = {{3{1'b0}}, isLsl};  // Bit_Extender bit_extender_6
  assign bit_extender_7_out = {{3{1'b0}}, isLsr};  // Bit_Extender bit_extender_7
  assign bit_extender_8_out = {{3{1'b0}}, isAsr};  // Bit_Extender bit_extender_8
  assign bit_extender_9_out = {{3{1'b0}}, isOr};  // Bit_Extender bit_extender_9
  assign bit_extender_10_out = {{3{1'b0}}, isNot};  // Bit_Extender bit_extender_10
  assign bit_extender_11_out = {{3{1'b0}}, isAnd};  // Bit_Extender bit_extender_11
  assign bit_extender_12_out = {{3{1'b0}}, isMov};  // Bit_Extender bit_extender_12
  assign bit_extender_13_out = {{3{1'b0}}, isAdd};  // Bit_Extender bit_extender_13
  Multiplier #(.width(4)) multiplier_1 (
    .a(bit_extender_1_out), .b(4'b0010), .out(multiplier_1_out));  // open: cin, cout
  Multiplier #(.width(4)) multiplier_2 (
    .a(bit_extender_2_out), .b(4'b0011), .out(multiplier_2_out));  // open: cin, cout
  Multiplier #(.width(4)) multiplier_3 (
    .a(bit_extender_3_out), .b(4'b0100), .out(multiplier_3_out));  // open: cin, cout
  Multiplier #(.width(4)) multiplier_4 (
    .a(bit_extender_4_out), .b(4'b0101), .out(multiplier_4_out));  // open: cin, cout
  Multiplier #(.width(4)) multiplier_5 (
    .a(bit_extender_5_out), .b(4'b0110), .out(multiplier_5_out));  // open: cin, cout
  Multiplier #(.width(4)) multiplier_6 (
    .a(bit_extender_6_out), .b(4'b0111), .out(multiplier_6_out));  // open: cin, cout
  Multiplier #(.width(4)) multiplier_7 (
    .a(bit_extender_7_out), .b(4'b1000), .out(multiplier_7_out));  // open: cin, cout
  Multiplier #(.width(4)) multiplier_8 (
    .a(bit_extender_8_out), .b(4'b1001), .out(multiplier_8_out));  // open: cin, cout
  Multiplier #(.width(4)) multiplier_9 (
    .a(bit_extender_9_out), .b(4'b1010), .out(multiplier_9_out));  // open: cin, cout
  Multiplier #(.width(4)) multiplier_10 (
    .a(bit_extender_10_out), .b(4'b1011), .out(multiplier_10_out));  // open: cin, cout
  Multiplier #(.width(4)) multiplier_11 (
    .a(bit_extender_11_out), .b(4'b1100), .out(multiplier_11_out));  // open: cin, cout
  Multiplier #(.width(4)) multiplier_12 (
    .a(bit_extender_12_out), .b(4'b1101), .out(multiplier_12_out));  // open: cin, cout
  Adder #(.width(4)) adder_1 (.a(bit_extender_13_out), .b(multiplier_1_out), .out(adder_1_out));  // open: cin, cout
  Adder #(.width(4)) adder_2 (.a(multiplier_2_out), .b(multiplier_3_out), .out(adder_2_out));  // open: cin, cout
  Adder #(.width(4)) adder_3 (.a(multiplier_4_out), .b(multiplier_5_out), .out(adder_3_out));  // open: cin, cout
  Adder #(.width(4)) adder_4 (.a(multiplier_6_out), .b(multiplier_7_out), .out(adder_4_out));  // open: cin, cout
  Adder #(.width(4)) adder_5 (.a(multiplier_8_out), .b(multiplier_9_out), .out(adder_5_out));  // open: cin, cout
  Adder #(.width(4)) adder_6 (.a(multiplier_10_out), .b(multiplier_11_out), .out(adder_6_out));  // open: cin, cout
  Adder #(.width(4)) adder_7 (.a(adder_1_out), .b(adder_2_out), .out(adder_7_out));  // open: cin, cout
  Adder #(.width(4)) adder_8 (.a(adder_3_out), .b(adder_4_out), .out(adder_8_out));  // open: cin, cout
  Adder #(.width(4)) adder_9 (.a(adder_5_out), .b(adder_6_out), .out(adder_9_out));  // open: cin, cout
  Adder #(.width(4)) adder_10 (.a(adder_7_out), .b(adder_8_out), .out(adder_10_out));  // open: cin, cout
  Adder #(.width(4)) adder_11 (.a(adder_9_out), .b(multiplier_12_out), .out(adder_11_out));  // open: cin, cout
  Adder #(.width(4)) adder_12 (.a(adder_10_out), .b(adder_11_out), .out(ALUSignals));  // open: cin, cout

  assign isImmediate = Instruction[26];

  // Notes on the sheet:
  //   Instruction: pull=down
  //   opcode
  //   (Circuit for signals created by multiple instructions)
  //   (Demultiplexer for Control Signals created by single instructions)
  //   Create ALUSignals
endmodule

module ALU (
  input  [31:0] A,
  input  [3:0] aluSignals,
  input  [31:0] B,
  input  clock,
  output [31:0] aluResult,
  output flags_GT,
  output flags_E
);

  wire [31:0] Add, addA, addB, And, andA, andB, Asr, asrA, asrB, cmpA, cmpB, Div, divA, divB, Lsl, lslA,
       lslB, Lsr, lsrA, lsrB, Mod, modA, modB, movB, Mul, mulA, mulB, Not, notB, Or, orA, orB, register_1_q,
       register_2_q, Sub, subA, subB;

  Demultiplexer #(.select(4), .width(32), .tristate("true"), .enable("false")) demultiplexer_1 (
    .out1(addA), .out2(subA), .out3(cmpA), .out4(mulA), .out5(divA), .out6(modA), .out7(lslA), .out8(lsrA),
    .out9(asrA), .out10(orA), .out12(andA), .in(A), .sel(aluSignals));  // open: out0, out11, out13, out14, out15
  Demultiplexer #(.select(4), .width(32), .tristate("true"), .disabled(0), .enable("false")) demultiplexer_2 (
    .out1(addB), .out2(subB), .out3(cmpB), .out4(mulB), .out5(divB), .out6(modB), .out7(lslB), .out8(lsrB),
    .out9(asrB), .out10(orB), .out11(notB), .out12(andB), .out13(movB), .in(B), .sel(aluSignals));  // open: out0, out14, out15
  Adder #(.width(32)) adder_1 (.a(addA), .b(addB), .out(Add));  // open: cin, cout
  Subtractor #(.width(32)) subtractor_1 (.a(subA), .b(subB), .out(Sub));  // open: bin, bout
  Shifter #(.width(32)) shifter_1 (.in(lslA), .\dist (lslB[4:0]), .out(Lsl));
  Shifter #(.width(32), .shift("lr")) shifter_2 (.in(lsrA), .\dist (lsrB[4:0]), .out(Lsr));
  Shifter #(.width(32), .shift("ar")) shifter_3 (.in(asrA), .\dist (asrB[4:0]), .out(Asr));
  Register #(.width(32)) register_1 (.D(cmpA), .Q(register_1_q), .clk(clock));  // open: en, clr
  Register #(.width(32)) register_2 (.D(cmpB), .Q(register_2_q), .clk(clock));  // open: en, clr
  Comparator #(.width(32)) comparator_1 (.a(register_1_q), .b(register_2_q), .gt(flags_GT), .eq(flags_E));  // open: lt
  Multiplier #(.width(32)) multiplier_1 (.a(mulA), .b(mulB), .out(Mul));  // open: cin, cout
  Divider #(.width(32)) divider_1 (.a(divA), .b(divB), .out(Div));  // open: upper, rem
  Divider #(.width(32)) divider_2 (.a(modA), .b(modB), .rem(Mod));  // open: out, upper
  Multiplexer #(.select(4), .width(32), .disabled(0)) multiplexer_1 (
    .in1(Add), .in2(Sub), .in4(Mul), .in5(Div), .in6(Mod), .in7(Lsl), .in8(Lsr), .in9(Asr), .in10(Or),
    .in11(Not), .in12(And), .in13(movB), .out(aluResult), .sel(aluSignals), .en(1'b1));  // open: in0, in3, in14, in15
  assign Or = orA | orB;  // OR_Gate or_1, 32 bits wide
  assign And = andA & andB;  // AND_Gate and_1, 32 bits wide
  assign Not = ~notB;  // NOT_Gate not_1, 32 bits wide

  // Notes on the sheet:
  //   aluResult: pull=down
  //   B: pull=down
  //   flags_GT: pull=down
  //   flags_E: pull=down
  //   A: pull=down
  //   Operand 1
  //   Operand 2
  //   Provide operands to their respective functions.
  //   Compare instruction needs registers as we need to keep the value of the flags stored.
endmodule

module EXU (
  input  isBeq,
  input  isUbranch,
  input  isBgt,
  input  isRet,
  input  [31:0] branchTargetIn,
  input  [1:0] Mux3,
  input  [31:0] A,
  input  [3:0] aluSignals,
  input  [31:0] MAData,
  input  Clock,
  input  [31:0] RWData,
  input  [1:0] Mux4,
  input  [31:0] B,
  output isBranchTaken,
  output [23:0] branchTargetOut,
  output [31:0] ALUResult
);

  wire and_1_out, and_2_out, flags_E, flags_GT;
  wire [31:0] multiplexer_1_out, multiplexer_2_out;
  wire [31:24] multiplexer_3_out;

  and and_1 (and_1_out, isBeq, flags_E);
  and and_2 (and_2_out, isBgt, flags_GT);
  Multiplexer #(.select(2), .width(32), .enable("false")) multiplexer_1 (
    .in0(A), .in1(MAData), .in2(RWData), .in3(MAData), .out(multiplexer_1_out), .sel(Mux3));
  Multiplexer #(.select(2), .width(32), .enable("false")) multiplexer_2 (
    .in0(B), .in1(MAData), .in2(RWData), .in3(MAData), .out(multiplexer_2_out), .sel(Mux4));
  or or_1 (isBranchTaken, and_1_out, isUbranch, and_2_out);
  ALU alu_1 (
    .A(multiplexer_1_out), .aluSignals(aluSignals), .B(multiplexer_2_out), .clock(Clock),
    .aluResult(ALUResult), .flags_GT(flags_GT), .flags_E(flags_E));
  Multiplexer #(.width(32), .enable("false")) multiplexer_3 (
    .in0(branchTargetIn), .in1(multiplexer_1_out), .out({multiplexer_3_out, branchTargetOut}), .sel(isRet));

  // Notes on the sheet:
  //   MAData: pull=down
  //   isBgt: pull=down
  //   A: pull=down
  //   branchTargetOut: pull=down
  //   aluSignals: pull=down
  //   B: pull=down
  //   isBeq: pull=down
  //   RWData: pull=down
  //   isBranchTaken: pull=down
  //   isUbranch: pull=down
  //   branchTargetIn: pull=down
  //   ALUResult: pull=down
  //   (Operand 1)
  //   (Operand 2)
  //   EX Stage
  //   (To be sent to the IF Stage)
endmodule

module DataLock (
  input  [31:0] A,
  input  [31:0] B,
  output src1Conflict,
  output src2Conflict
);

  wire and_1_out, and_2_out, and_3_out, comparator_1_eq, comparator_2_eq, demultiplexer_1_out8,
       demultiplexer_1_out9, demultiplexer_1_out13, demultiplexer_1_out16, demultiplexer_1_out17,
       demultiplexer_1_out18, demultiplexer_1_out19, demultiplexer_2_out5, demultiplexer_2_out13,
       demultiplexer_2_out15, demultiplexer_2_out16, demultiplexer_2_out17, demultiplexer_2_out18,
       demultiplexer_2_out20, hasSrc1, hasSrc2, isCall, isRet, isSt, or_1_out, or_2_out;
  wire [3:0] dest, src1, src2;

  Multiplexer #(.width(4), .enable("false")) multiplexer_1 (.in0(B[25:22]), .in1(4'b1111), .out(dest), .sel(isCall));
  Multiplexer #(.enable("false")) multiplexer_2 (.in0(1'b1), .in1(1'b0), .out(hasSrc2), .sel(and_1_out));
  and and_1 (and_1_out, ~isSt, A[26]);  // AND_Gate
  Multiplexer #(.width(4), .enable("false")) multiplexer_3 (.in0(A[21:18]), .in1(A[25:22]), .out(src1), .sel(isSt));
  Multiplexer #(.width(4), .enable("false")) multiplexer_4 (.in0(A[17:14]), .in1(4'b1111), .out(src2), .sel(isRet));
  Demultiplexer #(.select(5), .disabled(0), .enable("false")) demultiplexer_1 (
    .out8(demultiplexer_1_out8), .out9(demultiplexer_1_out9), .out13(demultiplexer_1_out13), .out15(isSt),
    .out16(demultiplexer_1_out16), .out17(demultiplexer_1_out17), .out18(demultiplexer_1_out18),
    .out19(demultiplexer_1_out19), .out20(isRet), .in(1'b1), .sel(A[31:27]));  // open: out0, out1, out2, out3, out4, out5, out6, out7, out10, out11, out12, out14, out21, out22, out23, out24, out25, out26, out27, out28, out29, out30, out31
  Demultiplexer #(.select(5), .disabled(0), .enable("false")) demultiplexer_2 (
    .out5(demultiplexer_2_out5), .out13(demultiplexer_2_out13), .out15(demultiplexer_2_out15),
    .out16(demultiplexer_2_out16), .out17(demultiplexer_2_out17), .out18(demultiplexer_2_out18),
    .out19(isCall), .out20(demultiplexer_2_out20), .in(1'b1), .sel(B[31:27]));  // open: out0, out1, out2, out3, out4, out6, out7, out8, out9, out10, out11, out12, out14, out21, out22, out23, out24, out25, out26, out27, out28, out29, out30, out31
  nor nor_1 (hasSrc1, demultiplexer_1_out8, demultiplexer_1_out9);
  or or_1 (or_1_out, demultiplexer_1_out13, demultiplexer_1_out16, demultiplexer_1_out17, demultiplexer_1_out18, demultiplexer_1_out19);
  Comparator #(.width(4), .mode("unsigned")) comparator_1 (.a(src1), .b(dest), .eq(comparator_1_eq));  // open: gt, lt
  Comparator #(.width(4), .mode("unsigned")) comparator_2 (.a(src2), .b(dest), .eq(comparator_2_eq));  // open: gt, lt
  or or_2 (or_2_out, demultiplexer_2_out5, demultiplexer_2_out13, demultiplexer_2_out15, demultiplexer_2_out16, demultiplexer_2_out17, demultiplexer_2_out18, demultiplexer_2_out20);
  and and_2 (and_2_out, hasSrc1, comparator_1_eq);
  and and_3 (and_3_out, comparator_2_eq, hasSrc2);
  and and_4 (src1Conflict, ~or_1_out, and_2_out, ~or_2_out);  // AND_Gate
  and and_5 (src2Conflict, ~or_1_out, and_3_out, ~or_2_out);  // AND_Gate

  // Other names for the same wires on the sheet: isImm = A[26]

  // Notes on the sheet:
  //   B: pull=down
  //   A: pull=down
  //   opcode
  //   Detect data lock
  //   opcode
endmodule

module Pipeline (
  input  [3:0] Register_Number,
  input  Reset
);

  wire and_1_out, Clock_out, Forwarding_Unit_mux2, Forwarding_Unit_mux5, isBranchTaken, isldUse, isWb, Mux1,
       Mux6, not_1_out, or_1_out;
  wire [1:0] Mux3, Mux4;
  wire [3:0] Control_2_q_2, Control_q_2, writeAddress;
  wire [12:0] Control, Control_3_q, Control_q;
  wire [12:1] Control_2_q;
  wire [23:0] branchPC, if_1_pc, PC_2_q, PC_3_q, PC_4_q, PC_q;
  wire [31:0] A_q, ALUResult_2_q, ALUResult_q, B_q, branchTarget_q, exu_1_aluresult, if_1_instruction,
       Instruction_2_q, Instruction_3_q, Instruction_4_q, Instruction_q, ldResult_q, ma_1_ldresult,
       multiplexer_1_out, multiplexer_2_out, Muxedop2, of_1_a, of_1_b, of_1_branchtarget, of_1_displayout,
       of_1_op2, op2_2_q, op2_q, writeData;

  not not_1 (not_1_out, isldUse);
  Clock Clock (.out(Clock_out));
  IF if_1 (
    .isBranchTaken(isBranchTaken), .Instruction(if_1_instruction), .branchTarget(branchPC),
    .IFstageclock(and_1_out), .PC(if_1_pc), .reset(Reset));
  and and_1 (and_1_out, not_1_out, Clock_out);
  MA ma_1 (
    .ldResult(ma_1_ldresult), .op2(op2_2_q), .isLd(Control_q[7]), .isSt(Control_q[12]),
    .ALUResult(ALUResult_q), .Clock(Clock_out), .Forwarded_Data(writeData), .Mux6(Mux6));
  Register #(.width(24)) PC (.D(PC_2_q), .Q(PC_q), .clk(Clock_out));  // open: en, clr
  EXU exu_1 (
    .isBeq(Control_3_q[8]), .isUbranch(Control_3_q[1]), .isBgt(Control_3_q[11]),
    .branchTargetIn(branchTarget_q), .A(A_q), .aluSignals(Control_3_q[6:3]), .B(B_q), .Clock(Clock_out),
    .isBranchTaken(isBranchTaken), .branchTargetOut(branchPC), .ALUResult(exu_1_aluresult),
    .isRet(Control_3_q[9]), .MAData(ALUResult_q), .RWData(writeData), .Mux3(Mux3), .Mux4(Mux4));
  Multiplexer #(.width(32), .enable("false")) multiplexer_1 (
    .in0(if_1_instruction), .in1(32'h68000000), .out(multiplexer_1_out), .sel(isBranchTaken));
  or or_1 (or_1_out, isldUse, isBranchTaken);
  Multiplexer #(.width(32), .enable("false")) multiplexer_2 (
    .in0(Instruction_q), .in1(32'h68000000), .out(multiplexer_2_out), .sel(or_1_out));
  Register #(.width(32)) Instruction (.D(multiplexer_1_out), .Q(Instruction_q), .clk(and_1_out));  // open: en, clr
  CU cu_1 (
    .isWb(Control[0]), .isUbranch(Control[1]), .isImmediate(Control[2]), .isLd(Control[7]),
    .isSt(Control[12]), .isBeq(Control[8]), .isBgt(Control[11]), .isCall(Control[10]), .isRet(Control[9]),
    .ALUSignals(Control[6:3]), .Instruction(Instruction_q));
  Register #(.width(24)) PC_2 (.D(if_1_pc), .Q(PC_2_q), .clk(and_1_out));  // open: en, clr
  Register #(.width(32)) Instruction_2 (.D(multiplexer_2_out), .Q(Instruction_2_q), .clk(Clock_out));  // open: en, clr
  Register #(.width(32)) ALUResult (.D(exu_1_aluresult), .Q(ALUResult_q), .clk(Clock_out));  // open: en, clr
  Register #(.width(32)) ldResult (.D(ma_1_ldresult), .Q(ldResult_q), .clk(Clock_out));  // open: en, clr
  Register #(.width(32)) A (.D(of_1_a), .Q(A_q), .clk(Clock_out));  // open: en, clr
  Register #(.width(24)) PC_3 (.D(PC_q), .Q(PC_3_q), .clk(Clock_out));  // open: en, clr
  Register #(.width(32)) ALUResult_2 (.D(ALUResult_q), .Q(ALUResult_2_q), .clk(Clock_out));  // open: en, clr
  Register #(.width(32)) op2 (.D(of_1_op2), .Q(op2_q), .clk(Clock_out));  // open: en, clr
  Register #(.width(32)) Instruction_3 (.D(Instruction_2_q), .Q(Instruction_3_q), .clk(Clock_out));  // open: en, clr
  Register #(.width(24)) PC_4 (.D(PC_3_q), .Q(PC_4_q), .clk(Clock_out));  // open: en, clr
  Register #(.width(32)) B (.D(of_1_b), .Q(B_q), .clk(Clock_out));  // open: en, clr
  Register #(.width(32)) op2_2 (.D(Muxedop2), .Q(op2_2_q), .clk(Clock_out));  // open: en, clr
  Register #(.width(32)) Instruction_4 (.D(Instruction_3_q), .Q(Instruction_4_q), .clk(Clock_out));  // open: en, clr
  Register #(.width(32)) branchTarget (.D(of_1_branchtarget), .Q(branchTarget_q), .clk(Clock_out));  // open: en, clr
  Register #(.width(13)) u_Control (
    .D(Control_3_q), .Q({Control_q[12:7], Control_q_2, Control_q[2:0]}), .clk(Clock_out));  // open: en, clr
  Register #(.width(13)) Control_2 (
    .D({Control_q[12:7], Control_q_2, Control_q[2:0]}),
    .Q({Control_2_q[12:7], Control_2_q_2, Control_2_q[2:1], isWb}), .clk(Clock_out));  // open: en, clr
  Register #(.width(13)) Control_3 (.D(Control), .Q(Control_3_q), .clk(Clock_out));  // open: en, clr
  OF of_1 (
    .Instruction(Instruction_q), .PC(PC_2_q), .branchTarget(of_1_branchtarget), .isSt(Control[12]),
    .isImmx(Control[2]), .A(of_1_a), .B(of_1_b), .op2(of_1_op2), .isRet(Control[9]), .writeData(writeData),
    .writeAddress(writeAddress), .isWb(isWb), .clock(Clock_out), .displayAddress(Register_Number),
    .displayOut(of_1_displayout), .isCall(Control[10]), .Mux2(Forwarding_Unit_mux2), .Mux1(Mux1));
  RW rw_1 (
    .Instruction(Instruction_4_q), .ldResult(ldResult_q), .isLd(Control_2_q[7]), .ALUResult(ALUResult_2_q),
    .isCall(Control_2_q[10]), .PC(PC_4_q), .Address(writeAddress), .storeData(writeData));
  ForwardingUnit Forwarding_Unit (
    .IF_OF_Packet(Instruction_q), .OF_EX_Packet(Instruction_2_q), .EX_MA_Packet(Instruction_3_q),
    .MA_RW_Packet(Instruction_4_q), .Mux3(Mux3), .Mux4(Mux4), .Mux1(Mux1), .Mux2(Forwarding_Unit_mux2),
    .Mux5(Forwarding_Unit_mux5), .Mux6(Mux6), .ldUseHazard(isldUse));
  Multiplexer #(.width(32), .enable("false")) multiplexer_3 (
    .in0(op2_q), .in1(writeData), .out(Muxedop2), .sel(Forwarding_Unit_mux5));
  Hex_Digit_Display hex_digit_display_1 (.value(of_1_displayout[31:28]));  // open: dp
  Hex_Digit_Display hex_digit_display_2 (.value(of_1_displayout[27:24]));  // open: dp
  Hex_Digit_Display hex_digit_display_3 (.value(of_1_displayout[23:20]));  // open: dp
  Hex_Digit_Display hex_digit_display_4 (.value(of_1_displayout[15:12]));  // open: dp
  Hex_Digit_Display hex_digit_display_5 (.value(of_1_displayout[19:16]));  // open: dp
  Hex_Digit_Display hex_digit_display_6 (.value(of_1_displayout[7:4]));  // open: dp
  Hex_Digit_Display hex_digit_display_7 (.value(of_1_displayout[11:8]));  // open: dp
  Hex_Digit_Display hex_digit_display_8 (.value(of_1_displayout[3:0]));  // open: dp

  // Other names for the same wires on the sheet: isCall = Control[10]

  // Notes on the sheet:
  //   OF / EX Register
  //   IF / OF Register
  //   MA / RW Register
  //   EX / MA Register
endmodule

module ForwardingUnit (
  input  [31:0] IF_OF_Packet,
  input  [31:0] OF_EX_Packet,
  input  [31:0] EX_MA_Packet,
  input  [31:0] MA_RW_Packet,
  output [1:0] Mux3,
  output [1:0] Mux4,
  output Mux1,
  output Mux2,
  output Mux5,
  output Mux6,
  output ldUseHazard
);

  wire datalock_1_src1conflict, datalock_1_src2conflict, datalock_2_src1conflict, datalock_2_src2conflict,
       datalock_3_src1conflict, datalock_3_src2conflict, datalock_4_src2conflict, datalock_5_src1conflict,
       datalock_5_src2conflict, exmaforwarding_1_out_3, or_1_out, rwexforwarding_1_out_3,
       rwexforwarding_2_out_3, rwexforwarding_3_out_3, rwmaforwarding_1_out_3, rwmaforwarding_2_out_3;

  DataLock datalock_1 (
    .A(OF_EX_Packet), .B(EX_MA_Packet), .src1Conflict(datalock_1_src1conflict),
    .src2Conflict(datalock_1_src2conflict));
  DataLock datalock_2 (
    .A(IF_OF_Packet), .B(MA_RW_Packet), .src1Conflict(datalock_2_src1conflict),
    .src2Conflict(datalock_2_src2conflict));
  DataLock datalock_3 (
    .A(OF_EX_Packet), .B(MA_RW_Packet), .src1Conflict(datalock_3_src1conflict),
    .src2Conflict(datalock_3_src2conflict));
  DataLock datalock_4 (
    .A(EX_MA_Packet), .B(MA_RW_Packet), .src2Conflict(datalock_4_src2conflict));  // open: src1Conflict
  DataLock datalock_5 (
    .A(IF_OF_Packet), .B(OF_EX_Packet), .src1Conflict(datalock_5_src1conflict),
    .src2Conflict(datalock_5_src2conflict));
  or or_1 (or_1_out, datalock_5_src2conflict, datalock_5_src1conflict);
  ExMaForwarding exmaforwarding_1 (.A(OF_EX_Packet), .B(EX_MA_Packet), .out_3(exmaforwarding_1_out_3));
  RwExForwarding rwexforwarding_1 (.A(IF_OF_Packet), .B(MA_RW_Packet), .out_3(rwexforwarding_1_out_3));
  RwExForwarding rwexforwarding_2 (.A(OF_EX_Packet), .B(MA_RW_Packet), .out_3(rwexforwarding_2_out_3));
  RwMaForwarding rwmaforwarding_1 (.A(EX_MA_Packet), .B(MA_RW_Packet), .out_3(rwmaforwarding_1_out_3));
  RwExForwarding rwexforwarding_3 (.A(IF_OF_Packet), .B(OF_EX_Packet), .out_3(rwexforwarding_3_out_3));
  and and_1 (Mux3[0], exmaforwarding_1_out_3, datalock_1_src1conflict);
  and and_2 (Mux4[0], exmaforwarding_1_out_3, datalock_1_src2conflict);
  and and_3 (Mux1, rwexforwarding_1_out_3, datalock_2_src1conflict);
  and and_4 (Mux2, rwexforwarding_1_out_3, datalock_2_src2conflict);
  RwMaForwarding rwmaforwarding_2 (.A(OF_EX_Packet), .B(MA_RW_Packet), .out_3(rwmaforwarding_2_out_3));
  and and_5 (Mux6, rwmaforwarding_1_out_3, datalock_4_src2conflict);
  and and_6 (ldUseHazard, rwexforwarding_3_out_3, or_1_out);
  and and_7 (Mux5, rwmaforwarding_2_out_3, datalock_3_src1conflict);
  and and_8 (Mux3[1], datalock_3_src1conflict, rwexforwarding_2_out_3);
  and and_9 (Mux4[1], rwexforwarding_2_out_3, datalock_3_src2conflict);

  // Notes on the sheet:
  //   MA_RW_Packet: pull=down
  //   EX_MA_Packet: pull=down
  //   IF_OF_Packet: pull=down
  //   OF_EX_Packet: pull=down
  //   Forwarding Unit
endmodule

module ExMaForwarding (
  input  [31:0] A,
  input  [31:0] B,
  output out_3
);

  wire demultiplexer_1_out0, demultiplexer_1_out1, demultiplexer_1_out2, demultiplexer_1_out3,
       demultiplexer_1_out4, demultiplexer_1_out5, demultiplexer_1_out6, demultiplexer_1_out7,
       demultiplexer_1_out8, demultiplexer_1_out9, demultiplexer_1_out10, demultiplexer_1_out11,
       demultiplexer_1_out12, demultiplexer_1_out14, demultiplexer_1_out15, demultiplexer_2_out0,
       demultiplexer_2_out1, demultiplexer_2_out2, demultiplexer_2_out3, demultiplexer_2_out4,
       demultiplexer_2_out6, demultiplexer_2_out7, demultiplexer_2_out8, demultiplexer_2_out9,
       demultiplexer_2_out10, demultiplexer_2_out11, demultiplexer_2_out12, or_1_out, or_2_out;

  Demultiplexer #(.select(5), .disabled(0), .enable("false")) demultiplexer_1 (
    .out0(demultiplexer_1_out0), .out1(demultiplexer_1_out1), .out2(demultiplexer_1_out2),
    .out3(demultiplexer_1_out3), .out4(demultiplexer_1_out4), .out5(demultiplexer_1_out5),
    .out6(demultiplexer_1_out6), .out7(demultiplexer_1_out7), .out8(demultiplexer_1_out8),
    .out9(demultiplexer_1_out9), .out10(demultiplexer_1_out10), .out11(demultiplexer_1_out11),
    .out12(demultiplexer_1_out12), .out14(demultiplexer_1_out14), .out15(demultiplexer_1_out15), .in(1'b1),
    .sel(A[31:27]));  // open: out13, out16, out17, out18, out19, out20, out21, out22, out23, out24, out25, out26, out27, out28, out29, out30, out31
  Demultiplexer #(.select(5), .disabled(0), .enable("false")) demultiplexer_2 (
    .out0(demultiplexer_2_out0), .out1(demultiplexer_2_out1), .out2(demultiplexer_2_out2),
    .out3(demultiplexer_2_out3), .out4(demultiplexer_2_out4), .out6(demultiplexer_2_out6),
    .out7(demultiplexer_2_out7), .out8(demultiplexer_2_out8), .out9(demultiplexer_2_out9),
    .out10(demultiplexer_2_out10), .out11(demultiplexer_2_out11), .out12(demultiplexer_2_out12), .in(1'b1),
    .sel(B[31:27]));  // open: out5, out13, out14, out15, out16, out17, out18, out19, out20, out21, out22, out23, out24, out25, out26, out27, out28, out29, out30, out31
  or or_1 (or_1_out, demultiplexer_1_out0, demultiplexer_1_out1, demultiplexer_1_out2, demultiplexer_1_out3, demultiplexer_1_out4, demultiplexer_1_out5, demultiplexer_1_out6, demultiplexer_1_out7, demultiplexer_1_out8, demultiplexer_1_out9, demultiplexer_1_out10, demultiplexer_1_out11, demultiplexer_1_out12, demultiplexer_1_out14, demultiplexer_1_out15);
  or or_2 (or_2_out, demultiplexer_2_out0, demultiplexer_2_out1, demultiplexer_2_out2, demultiplexer_2_out3, demultiplexer_2_out4, 1'b0, demultiplexer_2_out6, demultiplexer_2_out7, demultiplexer_2_out8, demultiplexer_2_out9, demultiplexer_2_out10, demultiplexer_2_out11, demultiplexer_2_out12);
  and and_1 (out_3, or_1_out, or_2_out);

  // Notes on the sheet:
  //   A: pull=down
  //   B: pull=down
endmodule

module RwMaForwarding (
  input  [31:0] A,
  input  [31:0] B,
  output out_3
);

  wire demultiplexer_1_out15, demultiplexer_2_out14;

  Demultiplexer #(.select(5), .disabled(0), .enable("false")) demultiplexer_1 (
    .out15(demultiplexer_1_out15), .in(1'b1), .sel(A[31:27]));  // open: out0, out1, out2, out3, out4, out5, out6, out7, out8, out9, out10, out11, out12, out13, out14, out16, out17, out18, out19, out20, out21, out22, out23, out24, out25, out26, out27, out28, out29, out30, out31
  Demultiplexer #(.select(5), .disabled(0), .enable("false")) demultiplexer_2 (
    .out14(demultiplexer_2_out14), .in(1'b1), .sel(B[31:27]));  // open: out0, out1, out2, out3, out4, out5, out6, out7, out8, out9, out10, out11, out12, out13, out15, out16, out17, out18, out19, out20, out21, out22, out23, out24, out25, out26, out27, out28, out29, out30, out31
  and and_1 (out_3, demultiplexer_1_out15, demultiplexer_2_out14);

  // Notes on the sheet:
  //   A: pull=down
  //   B: pull=down
endmodule

module RwExForwarding (
  input  [31:0] A,
  input  [31:0] B,
  output out_3
);

  wire demultiplexer_1_out0, demultiplexer_1_out1, demultiplexer_1_out2, demultiplexer_1_out3,
       demultiplexer_1_out4, demultiplexer_1_out5, demultiplexer_1_out6, demultiplexer_1_out7,
       demultiplexer_1_out8, demultiplexer_1_out9, demultiplexer_1_out10, demultiplexer_1_out11,
       demultiplexer_1_out12, demultiplexer_1_out14, demultiplexer_1_out15, demultiplexer_2_out14, or_1_out;

  Demultiplexer #(.select(5), .disabled(0), .enable("false")) demultiplexer_1 (
    .out0(demultiplexer_1_out0), .out1(demultiplexer_1_out1), .out2(demultiplexer_1_out2),
    .out3(demultiplexer_1_out3), .out4(demultiplexer_1_out4), .out5(demultiplexer_1_out5),
    .out6(demultiplexer_1_out6), .out7(demultiplexer_1_out7), .out8(demultiplexer_1_out8),
    .out9(demultiplexer_1_out9), .out10(demultiplexer_1_out10), .out11(demultiplexer_1_out11),
    .out12(demultiplexer_1_out12), .out14(demultiplexer_1_out14), .out15(demultiplexer_1_out15), .in(1'b1),
    .sel(A[31:27]));  // open: out13, out16, out17, out18, out19, out20, out21, out22, out23, out24, out25, out26, out27, out28, out29, out30, out31
  Demultiplexer #(.select(5), .disabled(0), .enable("false")) demultiplexer_2 (
    .out14(demultiplexer_2_out14), .in(1'b1), .sel(B[31:27]));  // open: out0, out1, out2, out3, out4, out5, out6, out7, out8, out9, out10, out11, out12, out13, out15, out16, out17, out18, out19, out20, out21, out22, out23, out24, out25, out26, out27, out28, out29, out30, out31
  or or_1 (or_1_out, demultiplexer_1_out0, demultiplexer_1_out1, demultiplexer_1_out2, demultiplexer_1_out3, demultiplexer_1_out4, demultiplexer_1_out5, demultiplexer_1_out6, demultiplexer_1_out7, demultiplexer_1_out8, demultiplexer_1_out9, demultiplexer_1_out10, demultiplexer_1_out11, demultiplexer_1_out12, demultiplexer_1_out14, demultiplexer_1_out15);
  and and_1 (out_3, or_1_out, demultiplexer_2_out14);

  // Notes on the sheet:
  //   A: pull=down
  //   B: pull=down
endmodule

module ForwardingUnit2 (
  input  [31:0] IF_OF_Packet,
  input  [31:0] OF_EX_Packet,
  input  [31:0] EX_MA_Packet,
  input  [31:0] MA_RW_Packet,
  output [1:0] Mux3,
  output [1:0] Mux4,
  output Mux1,
  output Mux2,
  output Mux5,
  output Mux6,
  output ldUseHazard
);

  wire datalock_1_src1conflict, datalock_1_src2conflict, datalock_5_src1conflict, datalock_5_src2conflict,
       not_1_out, or_1_out, rwexforwarding_1_out_3, rwmaforwarding_1_out_3;

  DataLock datalock_1 (
    .A(OF_EX_Packet), .B(EX_MA_Packet), .src1Conflict(datalock_1_src1conflict),
    .src2Conflict(datalock_1_src2conflict));
  DataLock datalock_2 (.A(IF_OF_Packet), .B(MA_RW_Packet), .src1Conflict(Mux1), .src2Conflict(Mux2));
  DataLock datalock_3 (.A(OF_EX_Packet), .B(MA_RW_Packet), .src1Conflict(Mux3[1]), .src2Conflict(Mux4[1]));
  DataLock datalock_4 (.A(EX_MA_Packet), .B(MA_RW_Packet), .src2Conflict(Mux6));  // open: src1Conflict
  DataLock datalock_5 (
    .A(IF_OF_Packet), .B(OF_EX_Packet), .src1Conflict(datalock_5_src1conflict),
    .src2Conflict(datalock_5_src2conflict));
  RwMaForwarding rwmaforwarding_1 (.out_3(rwmaforwarding_1_out_3));  // open: A, B
  or or_1 (or_1_out, datalock_5_src2conflict, datalock_5_src1conflict);
  not not_1 (not_1_out, rwmaforwarding_1_out_3);
  RwExForwarding rwexforwarding_1 (.A(IF_OF_Packet), .B(OF_EX_Packet), .out_3(rwexforwarding_1_out_3));
  and and_1 (Mux3[0], not_1_out, datalock_1_src1conflict);
  and and_2 (Mux4[0], not_1_out, datalock_1_src2conflict);
  and and_3 (ldUseHazard, rwexforwarding_1_out_3, or_1_out);

  assign Mux5 = Mux3[1];

  // Notes on the sheet:
  //   EX_MA_Packet: pull=down
  //   OF_EX_Packet: pull=down
  //   IF_OF_Packet: pull=down
  //   MA_RW_Packet: pull=down
  //   Forwarding Unit
endmodule
